# Fritzing sketch Schematc (saved by Fritzing 0.9.4)
breadboards: 1

parts:
  Componente2 = Arduino Uno (Rev3)
  DI1 = 16-segment display [package=THT]
  R1 = Resistor [tolerance=±5% resistance=220 package=THT]
  R2 = Resistor [tolerance=±5% resistance=220 package=THT]
  R3 = Resistor [tolerance=±5% resistance=220 package=THT]
  R4 = Resistor [tolerance=±5% resistance=220 package=THT]
  R5 = Resistor [tolerance=±5% resistance=220 package=THT]
  R6 = Resistor [tolerance=±5% resistance=220 package=THT]
  R7 = Resistor [tolerance=±5% resistance=220 package=THT]
  R8 = Resistor [tolerance=±5% resistance=220 package=THT]
  R9 = Resistor [tolerance=±5% resistance=220 package=THT]
  R10 = Resistor [tolerance=±5% resistance=220 package=THT]
  R11 = Resistor [tolerance=±5% resistance=220 package=THT]
  R12 = Resistor [tolerance=±5% resistance=220 package=THT]
  R13 = Resistor [tolerance=±5% resistance=220 package=THT]
  R14 = Resistor [tolerance=±5% resistance=220 package=THT]

nets:
  N1: Componente2.A0, R13.Pin_0
  N2: Componente2.A1, R12.Pin_0
  N3: Componente2.A2, R11.Pin_0
  N4: Componente2.A4/SDA, R10.Pin_0
  N5: Componente2.A5/SCL, DI1.anodeD1, R9.Pin_0
  N6: Componente2.D8, R7.Pin_1
  N7: Componente2.D9_PWM, R8.Pin_1
  N8: Componente2.D2, R1.Pin_1
  N9: Componente2.D3_PWM, R2.Pin_1
  N10: Componente2.D4, R3.Pin_1
  N11: Componente2.D5_PWM, R4.Pin_1
  N12: Componente2.D6_PWM, R5.Pin_1
  N13: Componente2.D7, R6.Pin_1
  N14: Componente2.3V3, R14.Pin_0
  N15: Componente2.GND, DI1.anodeD2
  N16: DI1.anodeA2, DI1.anodeK, R1.Pin_0
  N17: DI1.anodeA1, R2.Pin_0
  N18: DI1.anodeF, R3.Pin_0
  N19: DI1.anodeH, R4.Pin_0
  N20: DI1.anodeE, DI1.anodeB, R5.Pin_0
  N21: DI1.anodeJ, R6.Pin_0
  N22: DI1.anodeP, R7.Pin_0
  N23: DI1.anodeR, R8.Pin_0
  N24: DI1.anodeN, R9.Pin_1
  N25: DI1.commCathode#11, R14.Pin_1
  N26: DI1.anodeC, R10.Pin_1
  N27: DI1.anodeG, R13.Pin_1
  N28: DI1.anodeM, R12.Pin_1
  N29: DI1.commCathode#16, R11.Pin_1
